// Logisim project cpu.circ as structural Verilog: 13 circuits, main circuit main
module main (
  input  reset
);

  wire add, addi, ALUin, and_1_out, and_2_out, andOp, BLE, bne, check_negative_1_q, clk, DMwe, inp, j, JAL,
       JP, JR, keyboard_1_avail, lw, memory_latch_1_oe_latched, memory_latch_1_we_latched, nclk, not_2_out,
       notOp, or_3_out, outOp, Rdst, Rwe, shft, shftL, shftR, sixteen_bit_alu_1_z, sub;
  wire [1:0] ALUop;
  wire [2:0] multiplexer_1_out, multiplexer_3_out;
  wire [3:0] Opcode;
  wire [6:0] bit_extender_3_out, keyboard_1_data;
  wire [7:7] not_3_out;
  wire [11:0] Addr;
  wire [15:0] ALURes, bit_extender_1_out, bit_extender_2_out, bit_extender_4_out, left_shift_1_q, mem,
       memory_latch_1_address_latched, memory_latch_1_data_in_latched, multiplexer_2_out, multiplexer_4_out,
       multiplexer_5_out, multiplexer_6_out, multiplexer_7_out, multiplexer_9_out, multiplexer_10_out,
       multiplexer_11_out, multiplexer_12_out, multiplexer_13_out, PC_q, ram_1_dout, registerfile_1_rs2val,
       right_shift_1_out_3, RS1VAL, sixteen_bit_adder_1_result, sixteen_bit_adder_2_result;

  Clock u_clk (.out(clk));
  not not_1 (nclk, clk);
  indiv_reg PC (.Q(PC_q), .RST(reset), .CLK(nclk), .D(multiplexer_13_out), .WE(1'b1));
  sixteen_bit_adder sixteen_bit_adder_1 (
    .result(sixteen_bit_adder_1_result), .A(16'h1), .B(PC_q), .sub(1'b0));  // open: ovf
  ROM #(.addrWidth(16), .dataWidth(16)) rom_1 (.addr(PC_q), .data({Opcode, Addr}));
  Multiplexer #(.width(3), .enable("false")) multiplexer_1 (
    .in0(Addr[8:6]), .in1(Addr[5:3]), .out(multiplexer_1_out), .sel(Rdst));
  Multiplexer #(.width(16), .enable("false")) multiplexer_2 (
    .in0(multiplexer_11_out), .in1(sixteen_bit_adder_1_result), .out(multiplexer_2_out), .sel(JAL));
  Multiplexer #(.width(3), .enable("false")) multiplexer_3 (
    .in0(multiplexer_1_out), .in1(3'b111), .out(multiplexer_3_out), .sel(JAL));
  RegisterFile registerfile_1 (
    .RS1(Addr[11:9]), .RD(multiplexer_3_out), .RST(reset), .RDVAL(multiplexer_2_out),
    .RS2VAL(registerfile_1_rs2val), .RS1VAL(RS1VAL), .CLK(clk), .WE(Rwe), .RS2(Addr[8:6]));
  assign bit_extender_1_out = {{10{Addr[5]}}, Addr[5:0]};  // Bit_Extender bit_extender_1
  Multiplexer #(.width(16), .enable("false")) multiplexer_4 (
    .in0(registerfile_1_rs2val), .in1(bit_extender_1_out), .out(multiplexer_4_out), .sel(ALUin));
  Decoder #(.select(4), .enable("false")) decoder_1 (
    .out0(add), .out1(addi), .out2(sub), .out3(shftL), .out4(shftR), .out5(andOp), .out6(notOp), .out7(lw),
    .out8(DMwe), .out9(bne), .out10(BLE), .out11(j), .out12(JR), .out13(JAL), .out14(inp), .out15(outOp),
    .sel(Opcode));
  Multiplexer #(.width(16), .enable("false")) multiplexer_5 (
    .in0(RS1VAL), .in1(left_shift_1_q), .out(multiplexer_5_out), .sel(shftL));
  left_shift left_shift_1 (.A(RS1VAL), .Shamt(Addr[2:0]), .Q(left_shift_1_q));
  sixteen_bit_alu sixteen_bit_alu_1 (.Q(ALURes), .M(ALUop), .B(multiplexer_4_out), .A(RS1VAL), .Z(sixteen_bit_alu_1_z));
  sixteen_bit_adder sixteen_bit_adder_2 (
    .result(sixteen_bit_adder_2_result), .A(sixteen_bit_adder_1_result), .B(bit_extender_1_out), .sub(1'b0));  // open: ovf
  not not_2 (not_2_out, sixteen_bit_alu_1_z);
  right_shift right_shift_1 (.out_3(right_shift_1_out_3), .in_2(multiplexer_5_out), .in_1(Addr[2:0]));
  or or_1 (Rwe, add, addi, sub, shftL, shftR, andOp, notOp, lw, JAL, inp);
  Multiplexer #(.width(16), .enable("false")) multiplexer_6 (
    .in0(sixteen_bit_adder_1_result), .in1(sixteen_bit_adder_2_result), .out(multiplexer_6_out),
    .sel(and_1_out));
  and and_1 (and_1_out, bne, not_2_out);
  check_negative check_negative_1 (.Q(check_negative_1_q), .A(ALURes));
  Multiplexer #(.width(16), .enable("false")) multiplexer_7 (
    .in0(multiplexer_5_out), .in1(right_shift_1_out_3), .out(multiplexer_7_out), .sel(shftR));
  or or_2 (Rdst, add, sub, shftL, shftR, andOp, notOp, JR);
  or or_3 (or_3_out, sixteen_bit_alu_1_z, check_negative_1_q);
  Multiplexer #(.width(16), .enable("false")) multiplexer_8 (
    .in0(ALURes), .in1(multiplexer_7_out), .out(mem), .sel(shft));
  or or_4 (ALUin, addi, shftL, shftR, lw, DMwe, inp, outOp);
  Multiplexer #(.width(16), .enable("false")) multiplexer_9 (
    .in0(multiplexer_6_out), .in1(sixteen_bit_adder_2_result), .out(multiplexer_9_out), .sel(and_2_out));
  and and_2 (and_2_out, BLE, or_3_out);
  RAM #(.addrWidth(16), .dataWidth(16), .trigger("high"), .databus("bibus")) ram_1 (
    .addr(memory_latch_1_address_latched), .we(memory_latch_1_we_latched), .oe(memory_latch_1_oe_latched),
    .din(memory_latch_1_data_in_latched), .dout(ram_1_dout));
  memory_latch memory_latch_1 (
    .OE_latched(memory_latch_1_oe_latched), .address_latched(memory_latch_1_address_latched), .clk(nclk),
    .address(mem), .WE(DMwe), .data_in(registerfile_1_rs2val), .WE_latched(memory_latch_1_we_latched),
    .data_in_latched(memory_latch_1_data_in_latched));
  or or_5 (ALUop[1], andOp, notOp);
  or or_6 (ALUop[0], sub, notOp, bne, BLE);
  assign bit_extender_2_out = {{4{Addr[11]}}, Addr};  // Bit_Extender bit_extender_2
  Multiplexer #(.width(16), .enable("false")) multiplexer_10 (
    .in0(multiplexer_9_out), .in1(bit_extender_2_out), .out(multiplexer_10_out), .sel(JP));
  or or_7 (JP, j, JAL);
  Multiplexer #(.width(16), .enable("false")) multiplexer_11 (
    .in0(multiplexer_12_out), .in1(bit_extender_4_out), .out(multiplexer_11_out), .sel(inp));
  Multiplexer #(.width(16), .enable("false")) multiplexer_12 (
    .in0(memory_latch_1_address_latched), .in1(ram_1_dout), .out(multiplexer_12_out), .sel(lw));
  Keyboard keyboard_1 (.clk(nclk), .re(inp), .clr(reset), .avail(keyboard_1_avail), .data(keyboard_1_data));
  Multiplexer #(.width(16), .enable("false")) multiplexer_13 (
    .in0(multiplexer_10_out), .in1(RS1VAL), .out(multiplexer_13_out), .sel(JR));
  or or_8 (shft, shftL, shftR);
  not not_3 (not_3_out[7], keyboard_1_avail);
  Bit_Extender #(.in_width(16), .out_width(7)) bit_extender_3 (.in(RS1VAL), .out(bit_extender_3_out));
  TTY #(.rows(13), .cols(80)) tty_1 (.data(bit_extender_3_out), .clk(clk), .we(outOp), .clr(reset));
  assign bit_extender_4_out = {{8{not_3_out[7]}}, {not_3_out[7], keyboard_1_data}};  // Bit_Extender bit_extender_4

  // Other names for the same wires on the sheet: Imm[5:0] = Addr[5:0]; Shamt[2:0] = Addr[2:0]; Rd[2:0] = Addr[5:3];
  //   Rt[2:0] = Addr[8:6]; Rs[2:0] = Addr[11:9]; BR = bne; kbd = inp; Rwd = lw; rst = reset; shiftLeft = shftL;
  //   shiftRight = shftR; sw = DMwe; tty = outOp

  // Notes on the sheet:
  //   contents of rom_1 (hex, n*v repeats v):
  //   1083 10c4 1100 3825 1900 3825 1900 3821 1901 7940 7981 8880 88c1 1080 10c0 7880 78c1 a03f
endmodule

module indiv_reg (
  input  CLK,
  input  RST,
  input  WE,
  input  [15:0] D,
  output [15:0] Q
);

  wire and_1_out, and_2_out, and_3_out, and_4_out, and_5_out, and_6_out, and_7_out, and_8_out, and_9_out,
       and_10_out, and_11_out, and_12_out, and_13_out, and_14_out, and_15_out, and_16_out;

  and and_1 (and_1_out, WE, CLK);
  and and_2 (and_2_out, WE, CLK);
  and and_3 (and_3_out, WE, CLK);
  and and_4 (and_4_out, WE, CLK);
  D_Flip_Flop d_ff_1 (.D(D[0]), .clk(and_1_out), .Q(Q[0]), .reset(RST));  // open: Qn, preset
  D_Flip_Flop d_ff_2 (.D(D[4]), .clk(and_2_out), .Q(Q[4]), .reset(RST));  // open: Qn, preset
  D_Flip_Flop d_ff_3 (.D(D[8]), .clk(and_3_out), .Q(Q[8]), .reset(RST));  // open: Qn, preset
  D_Flip_Flop d_ff_4 (.D(D[12]), .clk(and_4_out), .Q(Q[12]), .reset(RST));  // open: Qn, preset
  // Probe on D[1]
  and and_5 (and_5_out, WE, CLK);
  and and_6 (and_6_out, WE, CLK);
  and and_7 (and_7_out, WE, CLK);
  and and_8 (and_8_out, WE, CLK);
  D_Flip_Flop d_ff_5 (.D(D[1]), .clk(and_5_out), .Q(Q[1]), .reset(RST));  // open: Qn, preset
  D_Flip_Flop d_ff_6 (.D(D[5]), .clk(and_6_out), .Q(Q[5]), .reset(RST));  // open: Qn, preset
  D_Flip_Flop d_ff_7 (.D(D[9]), .clk(and_7_out), .Q(Q[9]), .reset(RST));  // open: Qn, preset
  D_Flip_Flop d_ff_8 (.D(D[13]), .clk(and_8_out), .Q(Q[13]), .reset(RST));  // open: Qn, preset
  // Probe on Q[1]
  D_Flip_Flop d_ff_9 (.D(D[2]), .clk(and_9_out), .Q(Q[2]), .reset(RST));  // open: Qn, preset
  and and_9 (and_9_out, WE, CLK);
  D_Flip_Flop d_ff_10 (.D(D[6]), .clk(and_10_out), .Q(Q[6]), .reset(RST));  // open: Qn, preset
  and and_10 (and_10_out, WE, CLK);
  D_Flip_Flop d_ff_11 (.D(D[10]), .clk(and_11_out), .Q(Q[10]), .reset(RST));  // open: Qn, preset
  and and_11 (and_11_out, WE, CLK);
  D_Flip_Flop d_ff_12 (.D(D[14]), .clk(and_12_out), .Q(Q[14]), .reset(RST));  // open: Qn, preset
  and and_12 (and_12_out, WE, CLK);
  D_Flip_Flop d_ff_13 (.D(D[3]), .clk(and_13_out), .Q(Q[3]), .reset(RST));  // open: Qn, preset
  and and_13 (and_13_out, WE, CLK);
  D_Flip_Flop d_ff_14 (.D(D[7]), .clk(and_14_out), .Q(Q[7]), .reset(RST));  // open: Qn, preset
  and and_14 (and_14_out, WE, CLK);
  D_Flip_Flop d_ff_15 (.D(D[11]), .clk(and_15_out), .Q(Q[11]), .reset(RST));  // open: Qn, preset
  and and_15 (and_15_out, WE, CLK);
  D_Flip_Flop d_ff_16 (.D(D[15]), .clk(and_16_out), .Q(Q[15]), .reset(RST));  // open: Qn, preset
  and and_16 (and_16_out, WE, CLK);
endmodule

module RegisterFile (
  input  [15:0] RDVAL,
  input  CLK,
  input  RST,
  input  WE,
  input  [2:0] RD,
  input  [2:0] RS2,
  input  [2:0] RS1,
  output [15:0] RS1VAL,
  output [15:0] RS2VAL
);

  wire a0, a1, a2, a3, a4, a5, a6, a7, and_1_out, and_2_out, and_3_out, and_4_out, and_5_out, and_6_out,
       and_7_out, and_8_out, b0, b1, b2, b3, b4, b5, b6, b7, w0, w1, w2, w3, w4, w5, w6, w7;
  wire [15:0] indiv_reg_1_q, indiv_reg_2_q, indiv_reg_3_q, indiv_reg_4_q, indiv_reg_5_q, indiv_reg_6_q,
       indiv_reg_7_q, indiv_reg_8_q;

  Decoder #(.select(3), .enable("false")) decoder_1 (
    .out0(w0), .out1(w1), .out2(w2), .out3(w3), .out4(w4), .out5(w5), .out6(w6), .out7(w7), .sel(RD));
  Decoder #(.select(3), .enable("false")) decoder_2 (
    .out0(b0), .out1(b1), .out2(b2), .out3(b3), .out4(b4), .out5(b5), .out6(b6), .out7(b7), .sel(RS2));
  Decoder #(.select(3), .enable("false")) decoder_3 (
    .out0(a0), .out1(a1), .out2(a2), .out3(a3), .out4(a4), .out5(a5), .out6(a6), .out7(a7), .sel(RS1));
  // Probe on RDVAL
  and and_1 (and_1_out, CLK, WE, w0);
  and and_2 (and_2_out, CLK, WE, w1);
  and and_3 (and_3_out, CLK, WE, w2);
  and and_4 (and_4_out, CLK, WE, w3);
  indiv_reg indiv_reg_1 (.Q(indiv_reg_1_q), .RST(RST), .CLK(and_1_out), .D({16{1'b0}}), .WE(WE));
  // Probe on indiv_reg_1_q
  indiv_reg indiv_reg_2 (.Q(indiv_reg_2_q), .RST(RST), .CLK(and_2_out), .D(RDVAL), .WE(WE));
  // Probe on indiv_reg_2_q
  indiv_reg indiv_reg_3 (.Q(indiv_reg_3_q), .RST(RST), .CLK(and_3_out), .D(RDVAL), .WE(WE));
  // Probe on indiv_reg_3_q
  indiv_reg indiv_reg_4 (.Q(indiv_reg_4_q), .RST(RST), .CLK(and_4_out), .D(RDVAL), .WE(WE));
  // Probe on indiv_reg_4_q
  assign RS1VAL = a0 ? indiv_reg_1_q : 16'bz;  // Controlled_Buffer controlled_buffer_1
  assign RS2VAL = b0 ? indiv_reg_1_q : 16'bz;  // Controlled_Buffer controlled_buffer_2
  assign RS1VAL = a1 ? indiv_reg_2_q : 16'bz;  // Controlled_Buffer controlled_buffer_3
  assign RS2VAL = b1 ? indiv_reg_2_q : 16'bz;  // Controlled_Buffer controlled_buffer_4
  assign RS1VAL = a2 ? indiv_reg_3_q : 16'bz;  // Controlled_Buffer controlled_buffer_5
  assign RS2VAL = b2 ? indiv_reg_3_q : 16'bz;  // Controlled_Buffer controlled_buffer_6
  assign RS1VAL = a3 ? indiv_reg_4_q : 16'bz;  // Controlled_Buffer controlled_buffer_7
  assign RS2VAL = b3 ? indiv_reg_4_q : 16'bz;  // Controlled_Buffer controlled_buffer_8
  and and_5 (and_5_out, CLK, WE, w4);
  and and_6 (and_6_out, CLK, WE, w5);
  and and_7 (and_7_out, CLK, WE, w6);
  and and_8 (and_8_out, CLK, WE, w7);
  indiv_reg indiv_reg_5 (.Q(indiv_reg_5_q), .RST(RST), .CLK(and_5_out), .D(RDVAL), .WE(WE));
  // Probe on indiv_reg_5_q
  indiv_reg indiv_reg_6 (.Q(indiv_reg_6_q), .RST(RST), .CLK(and_6_out), .D(RDVAL), .WE(WE));
  // Probe on indiv_reg_6_q
  indiv_reg indiv_reg_7 (.Q(indiv_reg_7_q), .RST(RST), .CLK(and_7_out), .D(RDVAL), .WE(WE));
  // Probe on indiv_reg_7_q
  indiv_reg indiv_reg_8 (.Q(indiv_reg_8_q), .RST(RST), .CLK(and_8_out), .D(RDVAL), .WE(WE));
  // Probe on indiv_reg_8_q
  assign RS1VAL = a4 ? indiv_reg_5_q : 16'bz;  // Controlled_Buffer controlled_buffer_9
  assign RS2VAL = b4 ? indiv_reg_5_q : 16'bz;  // Controlled_Buffer controlled_buffer_10
  assign RS1VAL = a5 ? indiv_reg_6_q : 16'bz;  // Controlled_Buffer controlled_buffer_11
  assign RS2VAL = b5 ? indiv_reg_6_q : 16'bz;  // Controlled_Buffer controlled_buffer_12
  assign RS1VAL = a6 ? indiv_reg_7_q : 16'bz;  // Controlled_Buffer controlled_buffer_13
  assign RS2VAL = b6 ? indiv_reg_7_q : 16'bz;  // Controlled_Buffer controlled_buffer_14
  assign RS1VAL = a7 ? indiv_reg_8_q : 16'bz;  // Controlled_Buffer controlled_buffer_15
  assign RS2VAL = b7 ? indiv_reg_8_q : 16'bz;  // Controlled_Buffer controlled_buffer_16

  // Other names for the same wires on the sheet: data_in[15:0] = RDVAL; regA_out[15:0] = RS1VAL;
  //   regB_out[15:0] = RS2VAL
endmodule

module single_bit_adder (
  input  Cin,
  input  A,
  input  B,
  output Sum,
  output Cout
);

  wire and_1_out, and_2_out, xor_1_out;

  and and_1 (and_1_out, B, A);
  xor xor_1 (xor_1_out, A, B);
  or or_1 (Cout, and_1_out, and_2_out);
  and and_2 (and_2_out, xor_1_out, Cin);
  xor xor_2 (Sum, Cin, xor_1_out);
endmodule

module sixteen_bit_adder (
  input  sub,
  input  [15:0] A,
  input  [15:0] B,
  output ovf,
  output [15:0] result
);

  wire single_bit_adder_1_cout, single_bit_adder_2_cout, single_bit_adder_3_cout, single_bit_adder_4_cout,
       single_bit_adder_5_cout, single_bit_adder_6_cout, single_bit_adder_7_cout, single_bit_adder_8_cout,
       single_bit_adder_9_cout, single_bit_adder_10_cout, single_bit_adder_11_cout, single_bit_adder_12_cout,
       single_bit_adder_13_cout, single_bit_adder_14_cout, single_bit_adder_15_cout,
       single_bit_adder_16_cout, xor_1_out, xor_2_out, xor_3_out, xor_4_out, xor_5_out, xor_6_out, xor_7_out,
       xor_8_out, xor_9_out, xor_10_out, xor_11_out, xor_12_out, xor_13_out, xor_14_out, xor_15_out,
       xor_16_out;

  xor xor_1 (xor_1_out, B[0], sub);
  single_bit_adder single_bit_adder_1 (
    .Cin(sub), .A(A[0]), .B(xor_1_out), .Sum(result[0]), .Cout(single_bit_adder_1_cout));
  xor xor_2 (xor_2_out, B[1], sub);
  single_bit_adder single_bit_adder_2 (
    .Cin(single_bit_adder_1_cout), .A(A[1]), .B(xor_2_out), .Sum(result[1]), .Cout(single_bit_adder_2_cout));
  xor xor_3 (xor_3_out, B[2], sub);
  single_bit_adder single_bit_adder_3 (
    .Cin(single_bit_adder_2_cout), .A(A[2]), .B(xor_3_out), .Sum(result[2]), .Cout(single_bit_adder_3_cout));
  xor xor_4 (xor_4_out, B[3], sub);
  single_bit_adder single_bit_adder_4 (
    .Cin(single_bit_adder_3_cout), .A(A[3]), .B(xor_4_out), .Sum(result[3]), .Cout(single_bit_adder_4_cout));
  xor xor_5 (xor_5_out, B[4], sub);
  single_bit_adder single_bit_adder_5 (
    .Cin(single_bit_adder_4_cout), .A(A[4]), .B(xor_5_out), .Sum(result[4]), .Cout(single_bit_adder_5_cout));
  xor xor_6 (xor_6_out, B[5], sub);
  single_bit_adder single_bit_adder_6 (
    .Cin(single_bit_adder_5_cout), .A(A[5]), .B(xor_6_out), .Sum(result[5]), .Cout(single_bit_adder_6_cout));
  xor xor_7 (xor_7_out, B[6], sub);
  single_bit_adder single_bit_adder_7 (
    .Cin(single_bit_adder_6_cout), .A(A[6]), .B(xor_7_out), .Sum(result[6]), .Cout(single_bit_adder_7_cout));
  xor xor_8 (xor_8_out, B[7], sub);
  single_bit_adder single_bit_adder_8 (
    .Cin(single_bit_adder_7_cout), .A(A[7]), .B(xor_8_out), .Sum(result[7]), .Cout(single_bit_adder_8_cout));
  xor xor_9 (xor_9_out, B[8], sub);
  single_bit_adder single_bit_adder_9 (
    .Cin(single_bit_adder_8_cout), .A(A[8]), .B(xor_9_out), .Sum(result[8]), .Cout(single_bit_adder_9_cout));
  xor xor_10 (xor_10_out, B[9], sub);
  single_bit_adder single_bit_adder_10 (
    .Cin(single_bit_adder_9_cout), .A(A[9]), .B(xor_10_out), .Sum(result[9]), .Cout(single_bit_adder_10_cout));
  xor xor_11 (xor_11_out, B[10], sub);
  single_bit_adder single_bit_adder_11 (
    .Cin(single_bit_adder_10_cout), .A(A[10]), .B(xor_11_out), .Sum(result[10]),
    .Cout(single_bit_adder_11_cout));
  xor xor_12 (xor_12_out, B[11], sub);
  single_bit_adder single_bit_adder_12 (
    .Cin(single_bit_adder_11_cout), .A(A[11]), .B(xor_12_out), .Sum(result[11]),
    .Cout(single_bit_adder_12_cout));
  xor xor_13 (xor_13_out, B[12], sub);
  single_bit_adder single_bit_adder_13 (
    .Cin(single_bit_adder_12_cout), .A(A[12]), .B(xor_13_out), .Sum(result[12]),
    .Cout(single_bit_adder_13_cout));
  xor xor_14 (xor_14_out, B[13], sub);
  single_bit_adder single_bit_adder_14 (
    .Cin(single_bit_adder_13_cout), .A(A[13]), .B(xor_14_out), .Sum(result[13]),
    .Cout(single_bit_adder_14_cout));
  xor xor_15 (xor_15_out, B[14], sub);
  single_bit_adder single_bit_adder_15 (
    .Cin(single_bit_adder_14_cout), .A(A[14]), .B(xor_15_out), .Sum(result[14]),
    .Cout(single_bit_adder_15_cout));
  xor xor_16 (xor_16_out, B[15], sub);
  single_bit_adder single_bit_adder_16 (
    .Cin(single_bit_adder_15_cout), .A(A[15]), .B(xor_16_out), .Sum(result[15]),
    .Cout(single_bit_adder_16_cout));
  xor xor_17 (ovf, single_bit_adder_15_cout, single_bit_adder_16_cout);

  // Other names for the same wires on the sheet: S0 = result[0]; S1 = result[1]; S2 = result[2]; S3 = result[3];
  //   S4 = result[4]; S5 = result[5]; S6 = result[6]; S7 = result[7]; S8 = result[8]; S9 = result[9];
  //   S10 = result[10]; S11 = result[11]; S12 = result[12]; S13 = result[13]; S14 = result[14]; S15 = result[15]
endmodule

module memory_latch (
  input  [15:0] address,
  input  WE,
  input  clk,
  input  [15:0] data_in,
  output [15:0] address_latched,
  output WE_latched,
  output OE_latched,
  output [15:0] data_in_latched
);

  wire DMwe_latch_q;
  wire [15:0] addr_latch_q;

  Register #(.width(16), .trigger("falling")) addr_latch (
    .D(address), .en(WE), .clk(clk), .Q(addr_latch_q));  // open: clr
  D_Flip_Flop #(.trigger("falling")) DMwe_latch (.D(WE), .clk(clk), .Q(DMwe_latch_q));  // open: Qn, preset, reset
  Register #(.width(16), .trigger("falling")) data_to_be_written (
    .D(data_in), .en(WE), .clk(clk), .Q(data_in_latched));  // open: clr
  Multiplexer #(.width(16), .enable("false")) multiplexer_1 (
    .in0(address), .in1(addr_latch_q), .out(address_latched), .sel(DMwe_latch_q));
  and and_1 (WE_latched, clk, DMwe_latch_q);
  not not_1 (OE_latched, WE_latched);
endmodule

module single_bit_alu (
  input  A,
  input  B,
  input  C,
  input  [1:0] M,
  output Result,
  output Carry
);

  wire and_1_out, nor_1_out, single_bit_adder_1_sum, xor_1_out;
  wire [1:0] undriven;

  and and_1 (and_1_out, A, B);
  nor nor_1 (nor_1_out, A, B);
  xor xor_1 (xor_1_out, A, B);
  single_bit_adder single_bit_adder_1 (.Cin(C), .A(A), .B(B), .Sum(single_bit_adder_1_sum), .Cout(Carry));
  Multiplexer #(.select(2), .enable("false")) multiplexer_1 (
    .in0(single_bit_adder_1_sum), .in1(and_1_out), .in2(nor_1_out), .in3(xor_1_out), .out(Result),
    .sel(undriven));
endmodule

module sixteen_bit_alu (
  input  [15:0] A,
  input  [15:0] B,
  input  [1:0] M,
  output [15:0] Q,
  output Z
);

  wire or_1_out, or_2_out, or_3_out, or_4_out, or_5_out, or_6_out, or_7_out, or_8_out, or_9_out, or_10_out,
       or_11_out, or_12_out, or_13_out, or_14_out, or_15_out;
  wire [15:0] and_1_out, not_1_out, sixteen_bit_adder_1_result, sixteen_bit_adder_2_result;

  and and_1 (and_1_out[0], A[0], B[0]);
  and and_2 (and_1_out[1], A[1], B[1]);
  and and_3 (and_1_out[2], A[2], B[2]);
  and and_4 (and_1_out[3], A[3], B[3]);
  and and_5 (and_1_out[4], A[4], B[4]);
  and and_6 (and_1_out[5], A[5], B[5]);
  and and_7 (and_1_out[6], A[6], B[6]);
  and and_8 (and_1_out[7], A[7], B[7]);
  and and_9 (and_1_out[8], A[8], B[8]);
  and and_10 (and_1_out[9], A[9], B[9]);
  and and_11 (and_1_out[10], A[10], B[10]);
  and and_12 (and_1_out[11], A[11], B[11]);
  and and_13 (and_1_out[12], A[12], B[12]);
  and and_14 (and_1_out[13], A[13], B[13]);
  and and_15 (and_1_out[14], A[14], B[14]);
  and and_16 (and_1_out[15], A[15], B[15]);
  sixteen_bit_adder sixteen_bit_adder_1 (.result(sixteen_bit_adder_1_result), .A(A), .B(B), .sub(1'b0));  // open: ovf
  sixteen_bit_adder sixteen_bit_adder_2 (.result(sixteen_bit_adder_2_result), .A(A), .B(B), .sub(1'b1));  // open: ovf
  assign not_1_out = ~A;  // NOT_Gate not_1, 16 bits wide
  Multiplexer #(.select(2), .width(16), .enable("false")) multiplexer_1 (
    .in0(sixteen_bit_adder_1_result), .in1(sixteen_bit_adder_2_result), .in2(and_1_out), .in3(not_1_out),
    .out(Q), .sel(M));
  or or_1 (or_1_out, Q[0], Q[1]);
  or or_2 (or_2_out, or_1_out, or_3_out);
  or or_3 (or_3_out, Q[2], Q[3]);
  or or_4 (or_4_out, Q[4], Q[5]);
  or or_5 (or_5_out, or_4_out, or_6_out);
  or or_6 (or_6_out, Q[6], Q[7]);
  or or_7 (or_7_out, Q[8], Q[9]);
  or or_8 (or_8_out, or_7_out, or_9_out);
  or or_9 (or_9_out, Q[10], Q[11]);
  or or_10 (or_10_out, Q[12], Q[13]);
  or or_11 (or_11_out, or_10_out, or_12_out);
  or or_12 (or_12_out, Q[14], Q[15]);
  or or_13 (or_13_out, or_2_out, or_5_out);
  or or_14 (or_14_out, or_8_out, or_11_out);
  not not_2 (Z, or_15_out);
  or or_15 (or_15_out, or_13_out, or_14_out);
endmodule

module six_to_sixteen_extender (
  input  [5:0] A,
  output [15:0] Q
);


  assign Q = {{11{A[5]}}, A[4:0]};

  // Other names for the same wires on the sheet: extension = A[5]
endmodule

module left_shift (
  input  [2:0] Shamt,
  input  [15:0] A,
  output [15:0] Q
);

  BitSelector bitselector_1 (.in({{7{1'b0}}, A[0]}), .out(Q[0]), .sel(Shamt));
  BitSelector bitselector_2 (.in({{6{1'b0}}, A[0], A[1]}), .out(Q[1]), .sel(Shamt));
  BitSelector bitselector_3 (.in({{5{1'b0}}, A[0], A[1], A[2]}), .out(Q[2]), .sel(Shamt));
  BitSelector bitselector_4 (.in({4'b0000, A[0], A[1], A[2], A[3]}), .out(Q[3]), .sel(Shamt));
  BitSelector bitselector_5 (.in({3'b000, A[0], A[1], A[2], A[3], A[4]}), .out(Q[4]), .sel(Shamt));
  BitSelector bitselector_6 (.in({2'b00, A[0], A[1], A[2], A[3], A[4], A[5]}), .out(Q[5]), .sel(Shamt));
  BitSelector bitselector_7 (.in({1'b0, A[0], A[1], A[2], A[3], A[4], A[5], A[6]}), .out(Q[6]), .sel(Shamt));
  BitSelector bitselector_8 (.in({A[0], A[1], A[2], A[3], A[4], A[5], A[6], A[7]}), .out(Q[7]), .sel(Shamt));
  BitSelector bitselector_9 (.in({A[1], A[2], A[3], A[4], A[5], A[6], A[7], A[8]}), .out(Q[8]), .sel(Shamt));
  BitSelector bitselector_10 (.in({A[2], A[3], A[4], A[5], A[6], A[7], A[8], A[9]}), .out(Q[9]), .sel(Shamt));
  BitSelector bitselector_11 (.in({A[3], A[4], A[5], A[6], A[7], A[8], A[9], A[10]}), .out(Q[10]), .sel(Shamt));
  BitSelector bitselector_12 (.in({A[4], A[5], A[6], A[7], A[8], A[9], A[10], A[11]}), .out(Q[11]), .sel(Shamt));
  BitSelector bitselector_13 (.in({A[5], A[6], A[7], A[8], A[9], A[10], A[11], A[12]}), .out(Q[12]), .sel(Shamt));
  BitSelector bitselector_14 (.in({A[6], A[7], A[8], A[9], A[10], A[11], A[12], A[13]}), .out(Q[13]), .sel(Shamt));
  BitSelector bitselector_15 (.in({A[7], A[8], A[9], A[10], A[11], A[12], A[13], A[14]}), .out(Q[14]), .sel(Shamt));
  BitSelector bitselector_16 (.in({A[8], A[9], A[10], A[11], A[12], A[13], A[14], A[15]}), .out(Q[15]), .sel(Shamt));
endmodule

module twelve_to_sixteen_extender (
  input  [11:0] in_1,
  output [15:0] out_2
);


  assign out_2 = {{5{in_1[11]}}, in_1[10:0]};

  // Other names for the same wires on the sheet: extension = in_1[11]
endmodule

module right_shift (
  input  [2:0] in_1,
  input  [15:0] in_2,
  output [15:0] out_3
);

  BitSelector bitselector_1 (.in(in_2[7:0]), .out(out_3[0]), .sel(in_1));
  BitSelector bitselector_2 (.in(in_2[8:1]), .out(out_3[1]), .sel(in_1));
  BitSelector bitselector_3 (.in(in_2[9:2]), .out(out_3[2]), .sel(in_1));
  BitSelector bitselector_4 (.in(in_2[10:3]), .out(out_3[3]), .sel(in_1));
  BitSelector bitselector_5 (.in(in_2[11:4]), .out(out_3[4]), .sel(in_1));
  BitSelector bitselector_6 (.in(in_2[12:5]), .out(out_3[5]), .sel(in_1));
  BitSelector bitselector_7 (.in(in_2[13:6]), .out(out_3[6]), .sel(in_1));
  BitSelector bitselector_8 (.in(in_2[14:7]), .out(out_3[7]), .sel(in_1));
  BitSelector bitselector_9 (.in(in_2[15:8]), .out(out_3[8]), .sel(in_1));
  BitSelector bitselector_10 (.in({1'b0, in_2[15:9]}), .out(out_3[9]), .sel(in_1));
  BitSelector bitselector_11 (.in({2'b00, in_2[15:10]}), .out(out_3[10]), .sel(in_1));
  BitSelector bitselector_12 (.in({3'b000, in_2[15:11]}), .out(out_3[11]), .sel(in_1));
  BitSelector bitselector_13 (.in({4'b0000, in_2[15:12]}), .out(out_3[12]), .sel(in_1));
  BitSelector bitselector_14 (.in({{5{1'b0}}, in_2[15:13]}), .out(out_3[13]), .sel(in_1));
  BitSelector bitselector_15 (.in({{6{1'b0}}, in_2[15:14]}), .out(out_3[14]), .sel(in_1));
  BitSelector bitselector_16 (.in({{7{1'b0}}, in_2[15]}), .out(out_3[15]), .sel(in_1));

  // Other names for the same wires on the sheet: a0 = in_2[0]; a1 = in_2[1]; a2 = in_2[2]; a3 = in_2[3]; a4 = in_2[4];
  //   a5 = in_2[5]; a6 = in_2[6]; a7 = in_2[7]; a8 = in_2[8]; a9 = in_2[9]; a10 = in_2[10]; a11 = in_2[11];
  //   a12 = in_2[12]; a13 = in_2[13]; a14 = in_2[14]; a15 = in_2[15]; q0 = out_3[0]; q1 = out_3[1]; q2 = out_3[2];
  //   q3 = out_3[3]; q4 = out_3[4]; q5 = out_3[5]; q6 = out_3[6]; q7 = out_3[7]; q8 = out_3[8]; q9 = out_3[9];
  //   q10 = out_3[10]; q11 = out_3[11]; q12 = out_3[12]; q13 = out_3[13]; q14 = out_3[14]; q15 = out_3[15];
  //   shamt[2:0] = in_1
endmodule

module check_negative (
  input  [15:0] A,
  output Q
);


  assign Q = A[15];
endmodule
